# Fritzing sketch RPi-MCP3008-Pot_2 (saved by Fritzing 0.9.4)
breadboards: 1

parts:
  IC1 = MCP3008 8-channel 10-bit ADC [part_number=MCP3008]
  Raspberry_Pi_1 = Raspberry Pi 3 [part_number=RPI-3-V1.2]
  R2 = Resistor [tolerance=±5% resistance=220 package="0805 [SMD]"]
  R3 = Rotary Potentiometer (Large) [maximum_resistance=10kΩ package=THT]

nets:
  N1: IC1.no_name_yet#1, R2.Pin_0
  N2: IC1.no_name_yet#9, IC1.no_name_yet#14, Raspberry_Pi_1.GND, R3.leg1
  N3: IC1.no_name_yet#10, Raspberry_Pi_1.GPIO25
  N4: IC1.no_name_yet#11, Raspberry_Pi_1.GPIO24
  N5: IC1.no_name_yet#12, Raspberry_Pi_1.GPIO23
  N6: IC1.no_name_yet#13, Raspberry_Pi_1.GPIO18
  N7: IC1.no_name_yet#15, IC1.no_name_yet#16, Raspberry_Pi_1.3v3, R3.leg2
  N8: R2.Pin_1, R3.wiper
