# Fritzing sketch FONA.USB (saved by Fritzing 0.9.3b)
breadboards: 1

parts:
  Part1 = Adafruit FONA - Mini Cellular GSM Breakout
  Raspberry_Pi_1 = Raspberry Pi 3 [part_number=RPI-3-V1.2]
  U1 = LIPO-1000mAh [package=lipo-1000]
  USBTTL1 = USB TTL Serial Cable

nets:
  N1: Part1.GND#55, U1.-
  N2: Part1.VBAT#56, U1.+
  N3: Part1.VCCIO, Raspberry_Pi_1.3v3
  N4: Part1.RXD_5V, USBTTL1.TX
  N5: Part1.TXD_5V, USBTTL1.RX
  N6: Part1.PWRKEY_5V, Part1.GND#106, Raspberry_Pi_1.GND

notes:
  Using USB Cable

custom parts:
  Adafruit FONA - Mini Cellular GSM Breakout: An all-in-one cellular phone module that lets you add voice, text, SMS and GPRS data to your project. Quad-band 850/900/1800/1900MHz - connect onto any global GSM network with any 2G SIM. Includes an onboard LiPoly battery charging circuitry so you can take your project on the go. Also works as an FM radio receiver.
