# Fritzing sketch battery-fona (saved by Fritzing 0.9.3b)
circuit board: 5.1186cm x 3.5789cm
breadboards: 1

parts:
  IC1 = MCP3008 8-channel 10-bit ADC [part_number=MCP3008]
  Raspberry_Pi_B_rev2 = Raspberry Pi B rev2
  12v_input_to_monitor = Screw terminal - 2 pins [package=THT]
  R2 = Resistor [tolerance=±5% resistance=33k package="0805 [SMD]"]
  R1 = Resistor [tolerance=±5% resistance=100k package="0603 [SMD]"]
  POT1 = Breadboard Trimpot
  0-5v = Screw terminal - 2 pins [package=THT]
  Part2 = Adafruit FONA - Mini Cellular GSM Breakout
  U2 = LIPO-1000mAh [package=lipo-1000]  # not connected

nets:
  N1: IC1.no_name_yet#1, R2.Pin_0, R1.Pin_1
  GND: IC1.no_name_yet#9, IC1.no_name_yet#14, Raspberry_Pi_B_rev2.GPIO_3, Raspberry_Pi_B_rev2.GND, 12v_input_to_monitor.pin2, R2.Pin_1, 0-5v.pin2, Part2.PWRKEY_5V, Part2.GND
  N2: IC1.no_name_yet#10, IC1.no_name_yet#11, IC1.no_name_yet#15, IC1.no_name_yet#16, Raspberry_Pi_B_rev2.3V3, Raspberry_Pi_B_rev2.GPIO_24, Raspberry_Pi_B_rev2.GPIO_9, Raspberry_Pi_B_rev2.GPIO_25, Part2.VCCIO
  N3: IC1.no_name_yet#12, Raspberry_Pi_B_rev2.GPIO_23, Raspberry_Pi_B_rev2.GPIO_22
  N4: IC1.no_name_yet#13, Raspberry_Pi_B_rev2.GPIO_17, Raspberry_Pi_B_rev2.GPIO_18
  N5: Raspberry_Pi_B_rev2.GPIO_14, Part2.RXD_5V
  N6: Raspberry_Pi_B_rev2.GPIO_15, Part2.TXD_5V
  N7: 12v_input_to_monitor.pin1, R1.Pin_0, POT1.PIN2, POT1.PIN3, 0-5v.pin1

notes:
  See how to use it (from the software) at http://www.lediouris.net/RaspberryPI/ADC/monitor-12v.html
  Potentiometer to tune the tension to monitor
  Tension to monitor
  connected here =>
  Read the tuned tension here. This is the one that will feed the MCP3008.
  The connector is here just for a VoltMeter.

custom parts:
  Adafruit FONA - Mini Cellular GSM Breakout: An all-in-one cellular phone module that lets you add voice, text, SMS and GPRS data to your project. Quad-band 850/900/1800/1900MHz - connect onto any global GSM network with any 2G SIM. Includes an onboard LiPoly battery charging circuitry so you can take your project on the go. Also works as an FM radio receiver.
