# Fritzing sketch arduiono.fona (saved by Fritzing 0.9.3b)
breadboards: 2

parts:
  Part1 = Arduino Uno (Rev3)
  Part2 = Adafruit FONA - Mini Cellular GSM Breakout
  J1 = Screw terminal - 2 pins [package=THT]
  POT1 = Breadboard Trimpot
  J2 = Screw terminal - 2 pins [package=THT]
  R1 = Resistor [tolerance=±5% resistance=100k package="2512 [SMD]"]
  R2 = Resistor [tolerance=±5% resistance=33k package="2512 [SMD]"]

nets:
  N1: Part1.A0, R1.Pin_1, R2.Pin_0
  GND: Part1.GND, Part2.PWRKEY_5V, Part2.GND, J1.pin2, J2.pin2, R2.Pin_1
  N2: Part1.D2, Part2.RXD_5V
  N3: Part1.D3_PWM, Part2.TXD_5V
  N4: Part1.D4, Part2.RESET_5V
  N5: Part1.5V, Part2.VCCIO
  N6: J1.pin1, POT1.PIN2
  N7: POT1.PIN1, J2.pin1, R1.Pin_0

notes:
  Potentiometer, to tune the tension to monitior
  Connect the tension to monitor here
  Read the tension to monitor here, with a volt meter.

custom parts:
  Adafruit FONA - Mini Cellular GSM Breakout: An all-in-one cellular phone module that lets you add voice, text, SMS and GPRS data to your project. Quad-band 850/900/1800/1900MHz - connect onto any global GSM network with any 2G SIM. Includes an onboard LiPoly battery charging circuitry so you can take your project on the go. Also works as an FM radio receiver.
