# Fritzing sketch Arduino.HC-05.buzzer (saved by Fritzing 0.9.3b)

parts:
  Part1 = Bluetooth HC-05 Macho
  Part2 = Adafruit Metro with Headers [part_number="Adafruit #2488"]
  J1 = Piezo Speaker

nets:
  N1: Part1.TXD, Part2.IO2
  N2: Part1.RXD, Part2.IO3
  VCC: Part1.VCC, Part2.+5V
  GND: Part1.GND, Part2.GND, J1.pin1
  N3: Part2.IO8, J1.pin2

custom parts:
  Adafruit Metro with Headers: We sure love the ATmega328 here at Adafruit, and we use them a lot for our own projects. The processor has plenty of GPIO, Analog inputs, hardware UART SPI and I2C, timers and PWM galore - just enough for most simple projects. When we need to go small, we use a Pro Trinket 3V or 5V, but when size isn't as much of a concern, and an USB-serial converter is required, we reach for an Adafruit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
