# Fritzing sketch HC-SR04 (saved by Fritzing 0.9.3b)
breadboards: 1

parts:
  hc-sr1 = hc-sr04
  Raspberry_Pi_1 = Raspberry Pi 3 [part_number=RPI-3-V1.2]
  R1 = Resistor [tolerance=±5% resistance=330 package="0805 [SMD]"]
  R2 = Resistor [tolerance=±5% resistance=470 package="0805 [SMD]"]

nets:
  VCC: hc-sr1.VCC, Raspberry_Pi_1.5V
  N1: hc-sr1.Trig, Raspberry_Pi_1.GIPO23
  N2: hc-sr1.Echo, R1.Pin_0
  GND: hc-sr1.GND, Raspberry_Pi_1.GND, R2.Pin_1
  N3: Raspberry_Pi_1.GIPO24, R1.Pin_1, R2.Pin_0

notes:
  330 Ohms
  470 Ohms
