# Fritzing sketch Easy.Electronics.8 (saved by Fritzing 0.9.3b)
circuit board: 5.77145cm x 4.02166cm
breadboards: 1

parts:
  R1 = Resistor [tolerance=±5% resistance=100k package="0402 [SMD]"]
  IC1 = General purpose bipolar Timer [package=dil-08]
  R2 = Resistor [tolerance=±5% resistance=10k package="0402 [SMD]"]
  C1 = Capacitor Polarized [package=cpol-radial-10uf-25v]
  LED1 = LED - 5mm [color="Red (633nm)" package="5 mm [THT]"]
  BATT1 = 3xAAA Switchable Battery Pack w/JST connector

nets:
  N1: R1.Pin_0, IC1.DIS, R2.Pin_1
  N2: R1.Pin_1, IC1.TRI, IC1.TRE, C1.-
  N3: IC1.GND, C1.+, LED1.cathode, BATT1.NEG
  N4: IC1.OUT, LED1.anode
  N5: IC1.VCC+, R2.Pin_0, BATT1.POS

custom parts:
  3xAAA Switchable Battery Pack w/JST connector: 3xAAA Switchable Battery Pack with JST connector
