# Fritzing sketch MotorHat (saved by Fritzing 0.9.3b)

parts:
  Part1 = Adafruit DC+Stepper Motor HAT [part_number="Adafruit #2348"]
  Raspberry_Pi_1 = Raspberry Pi 3 [part_number=RPI-3-V1.2]
  M1 = Stepper Motor - Bipolar
  VCC1 = 4 x AAA Battery Mount

nets:
  N1: Part1.M2A, M1.D
  N2: Part1.M2B, M1.C
  N3: Part1.M1B, M1.A
  N4: Part1.M1A, M1.B
  GND: Part1.GND, Raspberry_Pi_1.GND, VCC1.-
  N5: Part1.VMOTOR, VCC1.+
  3V3: Part1.3.3V, Raspberry_Pi_1.3v3, Raspberry_Pi_1.3V3
  N6: Part1.5.0V, Raspberry_Pi_1.5V
  N7: Part1.SDA, Raspberry_Pi_1.GPIO2
  N8: Part1.SCL, Raspberry_Pi_1.GPIO3
  N9: Part1.GPIO4, Raspberry_Pi_1.GPIO4
  N10: Part1.TXD, Raspberry_Pi_1.GPIO14
  N11: Part1.RXD, Raspberry_Pi_1.GPIO15
  N12: Part1.GPIO17, Raspberry_Pi_1.GPIO17
  N13: Part1.GPIO18, Raspberry_Pi_1.GPIO18
  N14: Part1.GPIO27, Raspberry_Pi_1.GPIO27
  N15: Part1.GPIO22, Raspberry_Pi_1.GPIO22
  N16: Part1.GPIO23, Raspberry_Pi_1.GPIO23
  N17: Part1.GPIO24, Raspberry_Pi_1.GPIO24
  N18: Part1.SPI_MOSI, Raspberry_Pi_1.GPIO10
  N19: Part1.SPI_MISO, Raspberry_Pi_1.GPIO9
  N20: Part1.GPIO25, Raspberry_Pi_1.GPIO25
  N21: Part1.SPI_SCLK, Raspberry_Pi_1.GPIO11
  N22: Part1.SPI_CE0, Raspberry_Pi_1.GPIO8
  N23: Part1.SPI_CE1, Raspberry_Pi_1.GPIO7
  N24: Part1.EEDATA, Raspberry_Pi_1.ID_SD
  N25: Part1.EECLK, Raspberry_Pi_1.ID_SC
  N26: Part1.GPIO5, Raspberry_Pi_1.GPIO5
  N27: Part1.GPIO6, Raspberry_Pi_1.GPIO6
  N28: Part1.GPIO12, Raspberry_Pi_1.GPIO12
  N29: Part1.GPIO13, Raspberry_Pi_1.GPIO13
  N30: Part1.GPIO19, Raspberry_Pi_1.GPIO19
  N31: Part1.GPIO16, Raspberry_Pi_1.GPIO16
  N32: Part1.GPIO26, Raspberry_Pi_1.GPIO26
  N33: Part1.GPIO20, Raspberry_Pi_1.GPIO20
  N34: Part1.GPIO21, Raspberry_Pi_1.GPIO21

custom parts:
  Adafruit DC+Stepper Motor HAT: Let your robotic dreams come true with the new DC+Stepper Motor HAT from Adafruit. This Raspberry Pi add-on is perfect for any motion project as it can drive up to 4 DC or 2 Stepper motors with full PWM speed control. Since the Raspberry Pi does not have a lot of PWM pins, we use a fully-dedicated PWM driver chip onboard to both control motor direction and speed. This chip handles all the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
