# Fritzing sketch vl53l0x (saved by Fritzing 0.9.3b)
breadboards: 1

parts:
  Part1 = Adafruit VL53L0X Time of Flight Distance Sensor [part_number="Adafruit #3317"]
  Raspberry_Pi_1 = Raspberry Pi 3 [part_number=RPI-3-V1.2]

nets:
  VIN: Part1.VIN, Raspberry_Pi_1.5V
  GND: Part1.GND, Raspberry_Pi_1.GND
  N1: Part1.SCL, Raspberry_Pi_1.GPIO3
  N2: Part1.SDA, Raspberry_Pi_1.GPIO2

custom parts:
  Adafruit VL53L0X Time of Flight Distance Sensor: The VL53L0X is a Time of Flight distance sensor like no other you've used! The sensor contains a very tiny invisible laser source, and a matching sensor. The VL53L0X can detect the "time of flight", or how long the light has taken to bounce back to the sensor. Since it uses a very narrow light source, it is good for determining distance of only the surface directly in front of it. Unlike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
