# Fritzing sketch compass-mux-ext (saved by Fritzing 0.9.3b)
breadboards: 1

parts:
  Raspberry_Pi_Zero1 = Raspberry Pi Zero
  S1 = Pushbutton [package="[THT]"]
  Part2 = Triple Axis Magnetometer - HMC5883 Breakout
  Part3 = OLED Monochrome 128x32 I2C [part_number=931]

nets:
  N1: Raspberry_Pi_Zero1.GPIO2, Part2.SDA, Part3.SDA
  N2: Raspberry_Pi_Zero1.GPIO3, Part2.SCL, Part3.SCL
  N3: Raspberry_Pi_Zero1.3V3, S1.Pin_1, S1.Pin_2
  N4: Raspberry_Pi_Zero1.GPIO20, S1.Pin_3, S1.Pin_4
  GND: Raspberry_Pi_Zero1.GND, Part2.GND, Part3.GND
  5V: Raspberry_Pi_Zero1.5V, Part2.VCC, Part3.VIN

custom parts:
  OLED Monochrome 128x32 I2C: These displays are small, only about 1" diagonal, but very readable due to the high contrast of an OLED display. This display is made of 128x32 individual white OLED pixels, each one is turned on or off by the controller chip. Because the display makes its own light, no backlight is required. This reduces the power required to run the OLED and is why the display has such high contrast; we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
