# Fritzing sketch Two.RPi.Zero (saved by Fritzing 0.9.3b)
breadboards: 2

parts:
  Raspberry_Pi_Zero1 = Raspberry Pi Zero
  Raspberry_Pi_Zero2 = Raspberry Pi Zero
  Part1 = Adafruit BME280
  Part3 = HTU21D-F Temperature + Humidity Sensor
  Part4 = Adafruit BMP180

nets:
  N1: Raspberry_Pi_Zero1.GPIO2, Part1.SDI/SDA
  N2: Raspberry_Pi_Zero1.GPIO3, Part1.SCK/SCL
  3V3: Raspberry_Pi_Zero1.3V3, Part1.3.3V
  GND: Raspberry_Pi_Zero1.GND, Part1.GND
  N3: Raspberry_Pi_Zero2.GPIO2, Part3.SDA, Part4.SDA
  N4: Raspberry_Pi_Zero2.GPIO3, Part3.SCL, Part4.SCL
  +3V3: Raspberry_Pi_Zero2.3V3, Part3.+3V3, Part4.+3V3
  GND_2: Raspberry_Pi_Zero2.GND, Part3.GND, Part4.GND

custom parts:
  Adafruit BME280: Bosch has stepped up their game with their new BME280 sensor, an environmental sensor with temperature, barometric pressure and humidity! This sensor is great for all sorts of weather/environmental sensing and can even be used in both I2C and SPI! This precision sensor from Bosch is the best low-cost sensing solution for measuring humidity with ±3% accuracy, barometric pressure with ±1 hPa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
  HTU21D-F Temperature + Humidity Sensor: This I2C digital humidity sensor is an accurate and intelligent alternative to the much simpler Humidity and Temperature Sensor - SHT15 Breakout It has a typical accuracy of ±2% with an operating range that's optimized from 5% to 95% RH. Operation outside this range is still possible - just the accuracy might drop a bit. The temperature output has an accuracy of ±1°C from -30~90°C. If you're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
  Adafruit BMP180: This precision sensor from Bosch is the best low-cost sensing solution for measuring barometric pressure and temperature. Because pressure changes with altitude you can also use it as an altimeter! The sensor is soldered onto a PCB with a 3.3V regulator, I2C level shifter and pull-up resistors on the I2C pins. The BMP180 is the next-generation of sensors from Bosch, and replaces the BMP085.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
