# Fritzing sketch Adafruit.Ultimate.GPS.RPiZero.Bonnet.2 (saved by Fritzing 0.9.3b)
breadboards: 1

parts:
  Raspberry_Pi_Zero1 = Raspberry Pi Zero  # not connected
  Part3 = Adafruit Ultimate GPS v3 [part_number="Adafruit #746"]
  Part4 = Adafruit BME280

nets:
  GND: Part3.GND, Part4.GND

notes:
  Rx on the GPS goes on Tx on the Raspberry Pi
  Tx on the GPS goes on Rx on the Raspberry Pi
  Baud Rate is 9600

custom parts:
  Adafruit Ultimate GPS v3: We carry a few different GPS modules here in the Adafruit shop, but none that satisfied our every desire - that's why we designed this little GPS breakout board. We believe this is the Ultimate GPS module, so we named it that. It's got everything you want and more: -165 dBm sensitivity, 10 Hz updates, 66 channels 5V friendly design and only 20mA current draw Breadboard friendly + two mounting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
  Adafruit BME280: Bosch has stepped up their game with their new BME280 sensor, an environmental sensor with temperature, barometric pressure and humidity! This sensor is great for all sorts of weather/environmental sensing and can even be used in both I2C and SPI! This precision sensor from Bosch is the best low-cost sensing solution for measuring humidity with ±3% accuracy, barometric pressure with ±1 hPa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
