# Fritzing sketch perma-proto-pi-hat_tmp (saved by Fritzing 0.9.3b)

parts:
  Part1 = Adafruit Perma-Proto HAT [part_number="Adafruit #2314 and #2310"]
  Part2 = OLED Monochrome 128x64 1.3 inch [part_number=938]
  Part3 = Adafruit BME280
  S1 = Pushbutton [package="[THT]"]
  S2 = Pushbutton [package="[THT]"]

nets:
  N1: Part1.SDA, Part1.N$50#317
  N2: Part1.SCL, Part1.N$47#302
  N3: Part1.GPIO23, Part1.N$60#367
  N4: Part1.GPIO24, Part1.N$58#357
  N5: Part1.SPI_MOSI, Part1.N$61#372
  N6: Part1.SPI_SCLK, Part1.N$59#362
  N7: Part1.SPI_CE0, Part1.N$57#352
  N8: Part1.GPIO20, Part1.N$42#277
  N9: Part1.GPIO21, Part1.N$22#259
  N10: Part1.GND, Part1.N$46#297, Part1.N$53#332
  N11: Part1.3.3V, Part1.N$23#265, Part1.N$39#267, Part1.N$44#287, Part1.N$56#347
  N12: Part1.N$22#257, Part1.N$22#260, S2.Pin_3, S2.Pin_4
  N13: Part1.N$23#262, Part1.N$23#264, S2.Pin_1, S2.Pin_2
  N14: Part1.N$39#266, Part1.N$39#269, S1.Pin_1, S1.Pin_2
  N15: Part1.N$42#276, Part1.N$42#279, S1.Pin_3, S1.Pin_4
  N16: Part1.N$44#286, Part3.VIN
  N17: Part1.N$45#291, Part3.3.3V
  N18: Part1.N$46#296, Part3.GND
  N19: Part1.N$47#301, Part3.SCK/SCL
  N20: Part1.N$48#306, Part3.SDO/ADR
  N21: Part1.N$49#311, Part3.CS
  N22: Part1.N$50#316, Part3.SDI/SDA
  N23: Part1.N$53#331, Part2.GND
  N24: Part1.N$55, Part2.VIN
  N25: Part1.N$56#346, Part2.3.3V
  N26: Part1.N$57#351, Part2.CS
  N27: Part1.N$58#356, Part2.RESET
  N28: Part1.N$59#361, Part2.SCLK_SCK
  N29: Part1.N$60#366, Part2.DC_SA0
  N30: Part1.N$61#371, Part2.MOSI_SDA

custom parts:
  Adafruit Perma-Proto HAT: To kick off the Adafruit HAT party, we have this Perma-Proto inspired plug in daughter board. It has a grid of 0.1" prototyping soldering holes for attaching chips, resistors, LED, potentiometers and more. The holes are connected underneath with traces to mimic the solderless breadboards you're familiar. There's also long power strips for +3V, +5V and Ground connections to the Pi. Near the top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
  OLED Monochrome 128x64 1.3 inch: These displays are small, only about 1.3" diagonal, but very readable due to the high contrast of an OLED display. This display is made of 128x64 individual white OLED pixels, each one is turned on or off by the controller chip. Because the display makes its own light, no backlight is required. This reduces the power required to run the OLED and is why the display has such high contrast; we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
  Adafruit BME280: Bosch has stepped up their game with their new BME280 sensor, an environmental sensor with temperature, barometric pressure and humidity! This sensor is great for all sorts of weather/environmental sensing and can even be used in both I2C and SPI! This precision sensor from Bosch is the best low-cost sensing solution for measuring humidity with ±3% accuracy, barometric pressure with ±1 hPa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
