# Fritzing sketch ssd1306 (saved by Fritzing 0.9.3b)
breadboards: 1

parts:
  Raspberry_Pi_1 = Raspberry Pi 3 [part_number=RPI-3-V1.2]
  S1 = Momentary Switch [package=ksa_sealed_tac_switch]
  Part1 = OLED Monochrome 128x32 SPI [part_number=661]

nets:
  N1: Raspberry_Pi_1.3v3, S1.4
  N2: Raspberry_Pi_1.GIPO10, Part1.MOSI
  N3: Raspberry_Pi_1.GIPO11, Part1.SCLK
  N4: Raspberry_Pi_1.GIPO8, Part1.CS
  N5: Raspberry_Pi_1.GIPO24, Part1.RESET
  N6: Raspberry_Pi_1.GIPO23, Part1.DC
  N7: Raspberry_Pi_1.GIPO18, S1.2
  GND: Raspberry_Pi_1.GND, Part1.GND
  5V: Raspberry_Pi_1.5V, Part1.VIN

notes:
  OLED on 5v
  Switch on 3.3V

custom parts:
  OLED Monochrome 128x32 SPI: These displays are small, only about 1" diagonal, but very readable due to the high contrast of an OLED display. This display is made of 128x32 individual white OLED pixels, each one is turned on or off by the controller chip. Because the display makes its own light, no backlight is required. This reduces the power required to run the OLED and is why the display has such high contrast; we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
