# Fritzing sketch Arduino.STH10 (saved by Fritzing 0.9.3b)
breadboards: 1

parts:
  Part1 = Arduino Uno (Rev3)
  R1 = Resistor [tolerance=±5% resistance=10k package=THT]

nets:
  N1: Part1.D7, R1.Pin_0
  N2: Part1.3V3, R1.Pin_1

notes:
  Here go the connectors of the STH10. Yellow: SCL, blue: SDA, red: VCC and green: GND wires.
