# Fritzing sketch RaspberryPI.STH10 (saved by Fritzing 0.9.3b)
breadboards: 1

parts:
  R1 = Resistor [tolerance=±5% resistance=10k package=THT]
  Raspberry_Pi_1 = Raspberry Pi 3 [part_number=RPI-3-V1.2]
  Relay_5V1 = Keyes Relay [package=THT]  # not connected

nets:
  N1: R1.Pin_0, Raspberry_Pi_1.GPIO18
  N2: R1.Pin_1, Raspberry_Pi_1.3v3

notes:
  Here go the connectors of the STH10. Yellow: SCL, blue: SDA, red: VCC and green: GND wires.
  Works fine with the code at https://github.com/drohm/pi-sht1x (requires Python3), and the Java driver in this project.

custom parts:
  Keyes Relay: The Keyes 5V relay module is suitable for SCM development, home appliance control. It uses a 5V~12V TIL control signal which can control DC / AC signal.
