# Fritzing sketch MeArm (saved by Fritzing 0.9.3b)
breadboards: 1

parts:
  Part1 = 16-Channel 12-bit PWM Servo Driver - I2C [part_number=815]
  Raspberry_Pi_1 = Raspberry Pi 3 [part_number=RPI-3-V1.2]
  J1 = Basic Servo
  J2 = Basic Servo
  J3 = Basic Servo
  J4 = Basic Servo

nets:
  GND: Part1.GND, Raspberry_Pi_1.GND, J1.gnd, J2.gnd, J3.gnd, J4.gnd
  N1: Part1.PWM4, J4.pulse
  VCC: Part1.5.0V, J1.vcc, J2.vcc, J3.vcc, J4.vcc
  N2: Part1.PWM2, J3.pulse
  N3: Part1.PWM1, J2.pulse
  N4: Part1.PWM0, J1.pulse
  VCC_2: Part1.VCC, Raspberry_Pi_1.3v3
  N5: Part1.SDA, Raspberry_Pi_1.GPIO2
  N6: Part1.SCL, Raspberry_Pi_1.GPIO3

notes:
  Left
  Claw
  Bottom
  Right

custom parts:
  16-Channel 12-bit PWM Servo Driver - I2C: You want to make a cool robot, maybe a hexapod walker, or maybe just a piece of art with a lot of moving parts. Or maybe you want to drive a lot of LEDs with precise PWM output. Using only two pins, control 16 free-running PWM outputs! You can even chain up 62 breakouts to control up to 992 PWM outputs.
