# Fritzing sketch RPi-MCP3008-Joystick-servo (saved by Fritzing 0.9.3b)
breadboards: 1

parts:
  IC1 = MCP3008 8-channel 10-bit ADC [part_number=MCP3008]
  Raspberry_Pi_1 = Raspberry Pi 3 [part_number=RPI-3-V1.2]
  Part1 = 16-Channel 12-bit PWM Servo Driver - I2C [part_number=815]
  J1 = Basic Servo
  J2 = Basic Servo
  Part3 = Adafruit Analog 2-Axis Joystick [part_number="Adafruit #512"]

nets:
  GND: IC1.no_name_yet#9, IC1.no_name_yet#14, Raspberry_Pi_1.GND, Part1.GND, J1.gnd, J2.gnd, Part3.GND
  N1: IC1.no_name_yet#10, Raspberry_Pi_1.GPIO8
  N2: IC1.no_name_yet#11, Raspberry_Pi_1.GPIO10
  N3: IC1.no_name_yet#12, Raspberry_Pi_1.GPIO9
  N4: IC1.no_name_yet#13, Raspberry_Pi_1.GPIO11
  VCC: IC1.no_name_yet#15, IC1.no_name_yet#16, Raspberry_Pi_1.3v3, Part1.VCC, Part3.VCC
  N5: Raspberry_Pi_1.GPIO2, Part1.SDA
  N6: Raspberry_Pi_1.GPIO3, Part1.SCL
  VCC_2: Part1.5.0V, J1.vcc, J2.vcc
  N7: Part1.PWM1, J2.pulse
  N8: Part1.PWM0, J1.pulse

notes:
  PanTilt wiring.
  One servo for up-down
  One servo for left-right

custom parts:
  16-Channel 12-bit PWM Servo Driver - I2C: You want to make a cool robot, maybe a hexapod walker, or maybe just a piece of art with a lot of moving parts. Or maybe you want to drive a lot of LEDs with precise PWM output. Using only two pins, control 16 free-running PWM outputs! You can even chain up 62 breakouts to control up to 992 PWM outputs.
  Adafruit Analog 2-Axis Joystick: This mini-kit makes it easy to mount a PSP/Xbox-like thumb joystick to your project. The thumbstick is an analog joystick - more accurate and sensitive than just 'directional' joysticks - with a 'press in to select' button. Since it's analog, you'll need two analog reading pins on your microcontroller to determine X and Y. Having an extra digital input will let you read the switch. The pack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
