# Fritzing sketch RGBled (saved by Fritzing 0.9.3b)
breadboards: 1

parts:
  LED1 = RGB LED - (4 legs) [package="5 mm [THT]"]
  R1 = Resistor [tolerance=±5% resistance=150 package="0402 [SMD]"]
  R2 = Resistor [tolerance=±5% resistance=100 package="0402 [SMD]"]
  R3 = Resistor [tolerance=±5% resistance=100 package="0402 [SMD]"]
  Raspberry_Pi_1 = Raspberry Pi 3 [part_number=RPI-3-V1.2]

nets:
  N1: LED1.red_cathode, R1.Pin_0
  N2: LED1.common_anode, Raspberry_Pi_1.GND
  N3: LED1.green_cathode, R2.Pin_0
  N4: LED1.blue_cathode, R3.Pin_0
  N5: R1.Pin_1, Raspberry_Pi_1.GIPO17
  N6: R2.Pin_1, Raspberry_Pi_1.GIPO18
  N7: R3.Pin_1, Raspberry_Pi_1.GIPO27

notes:
  Resistors: between 100 and 150 Ω
