# Fritzing sketch 1-DC-motor (saved by Fritzing 0.9.3b)

parts:
  Part3 = Adafruit DC+Stepper Motor HAT [part_number="Adafruit #2348"]
  M1 = DC Motor

nets:
  N1: Part3.M1B, M1.pin_1
  N2: Part3.M1A, M1.pin_2

custom parts:
  Adafruit DC+Stepper Motor HAT: Let your robotic dreams come true with the new DC+Stepper Motor HAT from Adafruit. This Raspberry Pi add-on is perfect for any motion project as it can drive up to 4 DC or 2 Stepper motors with full PWM speed control. Since the Raspberry Pi does not have a lot of PWM pins, we use a fully-dedicated PWM driver chip onboard to both control motor direction and speed. This chip handles all the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
