# Fritzing sketch SparkFunSoilMoisture (saved by Fritzing 0.9.3b)
breadboards: 1

parts:
  Part1 = Soil Moisture Sensor
  IC1 = MCP3008 8-channel 10-bit ADC [part_number=MCP3008]
  Raspberry_Pi_Zero1 = Raspberry Pi Zero
  Relay_5V2 = Keyes Relay [package=THT]
  VCC2 = Battery block 9V

nets:
  GND: Part1.GND, IC1.no_name_yet#9, IC1.no_name_yet#14, Raspberry_Pi_Zero1.GND, Relay_5V2.ground
  3V3: Part1.VCC, IC1.no_name_yet#15, IC1.no_name_yet#16, Raspberry_Pi_Zero1.3v3, Raspberry_Pi_Zero1.3V3, Relay_5V2.signal
  N1: IC1.no_name_yet#10, Raspberry_Pi_Zero1.GPIO25
  N2: IC1.no_name_yet#11, Raspberry_Pi_Zero1.GPIO24
  N3: IC1.no_name_yet#12, Raspberry_Pi_Zero1.GPIO23
  N4: IC1.no_name_yet#13, Raspberry_Pi_Zero1.GPIO18
  N5: Raspberry_Pi_Zero1.GPIO17, Relay_5V2.power
  N6: Relay_5V2.C, VCC2.+

notes:
  Relay's VCC goes on 3.3V
  12 V
  To the Pump

custom parts:
  Keyes Relay: The Keyes 5V relay module is suitable for SCM development, home appliance control. It uses a 5V~12V TIL control signal which can control DC / AC signal.
