# Fritzing sketch LightSensorWiring (saved by Fritzing 0.9.3b)
breadboards: 1

parts:
  IC1 = MCP3008 8-channel 10-bit ADC [part_number=MCP3008]
  Raspberry_Pi_Zero1 = Raspberry Pi Zero
  R1 = PHOTOCELL [package=photocell]
  R2 = Resistor [tolerance=±5% resistance=10k package="2512 [SMD]"]

nets:
  N1: IC1.no_name_yet#9, IC1.no_name_yet#14, Raspberry_Pi_Zero1.GND, R2.Pin_0
  N2: IC1.no_name_yet#10, Raspberry_Pi_Zero1.GPIO25
  N3: IC1.no_name_yet#11, Raspberry_Pi_Zero1.GPIO24
  N4: IC1.no_name_yet#12, Raspberry_Pi_Zero1.GPIO23
  N5: IC1.no_name_yet#13, Raspberry_Pi_Zero1.GPIO18
  N6: IC1.no_name_yet#15, IC1.no_name_yet#16, Raspberry_Pi_Zero1.3v3, R1.P$2
  N7: R1.P$1, R2.Pin_1

notes:
  10K Ohm resistor to the ground
