# Fritzing sketch rpi.radar.serial (saved by Fritzing 0.9.3b)
breadboards: 1

parts:
  Part1 = 16-Channel 12-bit PWM Servo Driver - I2C [part_number=815]
  Raspberry_Pi_1 = Raspberry Pi 3 [part_number=RPI-3-V1.2]
  hc-sr1 = hc-sr04
  J2 = Basic Servo
  USBTTL2 = USB TTL Serial Cable

nets:
  GND: Part1.GND, Raspberry_Pi_1.GND, hc-sr1.GND, J2.gnd, USBTTL2.GND
  VCC: Part1.VCC, Raspberry_Pi_1.3v3
  N1: Part1.5.0V, J2.pulse
  N2: Part1.SDA, Raspberry_Pi_1.GPIO2
  N3: Part1.SCL, Raspberry_Pi_1.GPIO3
  N4: Part1.PWM15, J2.vcc
  N5: Raspberry_Pi_1.GPIO24, hc-sr1.Echo
  N6: Raspberry_Pi_1.GPIO23, hc-sr1.Trig
  N7: Raspberry_Pi_1.GPIO15, USBTTL2.TX
  N8: Raspberry_Pi_1.GPIO14, USBTTL2.RX
  5V: Raspberry_Pi_1.5V, hc-sr1.VCC

notes:
  5V power
  supply
  The servo is orienting the HC-SR04
  Plug the USB
  into your laptop

custom parts:
  16-Channel 12-bit PWM Servo Driver - I2C: You want to make a cool robot, maybe a hexapod walker, or maybe just a piece of art with a lot of moving parts. Or maybe you want to drive a lot of LEDs with precise PWM output. Using only two pins, control 16 free-running PWM outputs! You can even chain up 62 breakouts to control up to 992 PWM outputs.
