# Fritzing sketch RPi-MCP3008-2-Pots (saved by Fritzing 0.9.3b)
breadboards: 1

parts:
  IC1 = MCP3008 8-channel 10-bit ADC [part_number=MCP3008]
  Raspberry_Pi_1 = Raspberry Pi 3 [part_number=RPI-3-V1.2]
  R2 = Resistor [tolerance=±5% resistance=220 package="0805 [SMD]"]
  R3 = Rotary Potentiometer (Large) [maximum_resistance=10kΩ package=THT]
  R4 = Rotary Potentiometer (Large) [maximum_resistance=10kΩ package=THT]
  R5 = Resistor [tolerance=±5% resistance=220 package="0805 [SMD]"]
  Part1 = 16-Channel 12-bit PWM Servo Driver - I2C [part_number=815]
  J1 = Basic Servo

nets:
  GND: IC1.no_name_yet#9, IC1.no_name_yet#14, Raspberry_Pi_1.GND, R3.leg1, R4.leg1, Part1.GND, J1.gnd
  N1: IC1.no_name_yet#10, Raspberry_Pi_1.GPIO25
  N2: IC1.no_name_yet#11, Raspberry_Pi_1.GPIO10
  N3: IC1.no_name_yet#12, Raspberry_Pi_1.GPIO9
  N4: IC1.no_name_yet#13, Raspberry_Pi_1.GPIO11
  3V3: IC1.no_name_yet#15, IC1.no_name_yet#16, Raspberry_Pi_1.3v3, R3.leg2, R4.leg2, Part1.VCC
  N5: Raspberry_Pi_1.GPIO2, Part1.SDA
  N6: Raspberry_Pi_1.GPIO3, Part1.SCL
  N7: Raspberry_Pi_1.5V, Part1.PWRIN
  N8: R2.Pin_1, R3.wiper
  N9: R4.wiper, R5.Pin_0
  N10: Part1.PWM1, J1.pulse
  N11: Part1.5.0V, J1.vcc

notes:
  Knob
  Feedback

custom parts:
  16-Channel 12-bit PWM Servo Driver - I2C: You want to make a cool robot, maybe a hexapod walker, or maybe just a piece of art with a lot of moving parts. Or maybe you want to drive a lot of LEDs with precise PWM output. Using only two pins, control 16 free-running PWM outputs! You can even chain up 62 breakouts to control up to 992 PWM outputs.
