# Fritzing sketch PWM.servo (saved by Fritzing 0.9.3b)

parts:
  Raspberry_Pi_1 = Raspberry Pi 3 [part_number=RPI-3-V1.2]
  J1 = Basic Servo

nets:
  N1: Raspberry_Pi_1.GIPO18, J1.pulse
  GND: Raspberry_Pi_1.GND, J1.gnd
  5V: Raspberry_Pi_1.5V, J1.vcc

notes:
  Servo on GPIO_01 here
  Physical pin #12,
  BMC 18
