# Fritzing sketch RaspberryPI.STH10 (saved by Fritzing 0.9.3b)
breadboards: 1

parts:
  R1 = Resistor [tolerance=±5% resistance=10k package=THT]
  Raspberry_Pi_1 = Raspberry Pi 3 [part_number=RPI-3-V1.2]
  Relay_5V1 = Keyes Relay [package=THT]
  VALVE1 = Plastic Solenoid Valve
  U1 = SHT1x Humdity Sensor [package=sht1x]
  VCC1 = Battery block 9V

nets:
  N1: R1.Pin_0, Raspberry_Pi_1.GPIO18, U1.DATA
  3V3: R1.Pin_1, Raspberry_Pi_1.3v3, Raspberry_Pi_1.3V3, Relay_5V1.signal, U1.VDD
  N2: Raspberry_Pi_1.GPIO17, Relay_5V1.power
  N3: Raspberry_Pi_1.GPIO23, U1.SCK
  GND: Raspberry_Pi_1.GND, Relay_5V1.ground, U1.GND
  N4: Relay_5V1.C, VCC1.+
  N5: Relay_5V1.NO, VALVE1.no_name_yet

notes:
  Here go the connectors of the STH10. Yellow: SCL, blue: SDA, red: VCC and green: GND wires.
  Works fine with the code at https://github.com/drohm/pi-sht1x (requires Python3), and the Java driver in this project.
  Make sure the wiring corresponds to your relay:
  Orange: SIGNAL
  Red: POWER
  Black: GROUND
  12 V
  Relay's VCC goes on 3.3V

custom parts:
  Keyes Relay: The Keyes 5V relay module is suitable for SCM development, home appliance control. It uses a 5V~12V TIL control signal which can control DC / AC signal.
