# Fritzing sketch SparkFun.Bonnet (saved by Fritzing 0.9.3b)
breadboards: 1

parts:
  Raspberry_Pi_Zero1 = Raspberry Pi Zero  # not connected
  IC1 = MCP3008 8-channel 10-bit ADC [part_number=MCP3008]
  Part2 = Soil Moisture Sensor
  KY-1 = Keyes Relay [package=THT]
  Part3 = Lilypad Power Supply
  J2 = Screw terminal - 2 pins [package=THT]
  J3 = Screw terminal - 2 pins [package=THT]
  Part4 = PowerBoost 500 Basic
  U1 = LIPO-2000mAh [package=lipo-2000]  # not connected
  C1 = Electrolytic Capacitor [capacitance=1000µF package="300 mil [THT, electrolytic]"]
  C2 = Electrolytic Capacitor [capacitance=1000µF package="300 mil [THT, electrolytic]"]
  JP3 = Header 3 [package=screwterminal-3.5mm-3_lock.007s]
  JP1 = Header 3 [package=screwterminal-3.5mm-3_lock.007s]

nets:
  N1: IC1.no_name_yet#1, Part2.SIG, JP3.2
  GND: IC1.no_name_yet#9, IC1.no_name_yet#14, Part2.GND, KY-1.ground, Part3.GND, J2.pin2, J3.pin1, Part4.GND, C1.-, C2.-, JP1.1
  N2: IC1.no_name_yet#15, IC1.no_name_yet#16, Part2.VCC, KY-1.signal, J3.pin2, JP3.1
  N3: KY-1.C, Part3.+, J2.pin1, Part4.5.0V, C1.+, JP1.2
  N4: KY-1.NO, C2.+, JP1.3

notes:
  5v Water pump
  + -
  5v Power Supply
  Raspberry Pi Zero under the Adafruit Bonnet. Powered by the Bonnet.
  Notice the PowerBoost (500) and the LiPo battery.
  The power supply is powering the booster, that in turn powers the Raspberry Pi, through the its battery.
  The reason for that is that it is difficult (if even possible) to power the Raspberry Pi and the Pump from the same 5v source. When the pump starts, this generates a voltage drop that makes the Raspberry Pi reboot...
  In this configuration, the booster and its LiPo battery are acting as a buffer on the power supply line.
  The two 1000µF capacitors are here to smooth the surge of both the pump and the booster.
  1000µF capacitor
  Connections to the outside world

custom parts:
  Keyes Relay: The Keyes 5V relay module is suitable for SCM development, home appliance control. It uses a 5V~12V TIL control signal which can control DC / AC signal.
  PowerBoost 500 Basic: The PowerBoost 500 Basic is a little DC/DC boost converter module that can run from 1.8V batteries or higher, and convert the battery output to 5.2V DC for running your 5V projects. At its heart is a TPS61090 boost converter from TI. This boost converter chip has some really nice extras such as low battery detection, 2A internal switch, synchronous conversion, excellent efficiency, and 700KHz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
