# Fritzing sketch SparkFunSoilMoisture (saved by Fritzing 0.9.3b)
breadboards: 1

parts:
  Part1 = Soil Moisture Sensor
  IC1 = MCP3008 8-channel 10-bit ADC [part_number=MCP3008]
  Raspberry_Pi_Zero1 = Raspberry Pi Zero

nets:
  GND: Part1.GND, IC1.no_name_yet#9, IC1.no_name_yet#14, Raspberry_Pi_Zero1.GND
  VCC: Part1.VCC, IC1.no_name_yet#15, IC1.no_name_yet#16, Raspberry_Pi_Zero1.3v3
  N1: IC1.no_name_yet#10, Raspberry_Pi_Zero1.GPIO25
  N2: IC1.no_name_yet#11, Raspberry_Pi_Zero1.GPIO24
  N3: IC1.no_name_yet#12, Raspberry_Pi_Zero1.GPIO23
  N4: IC1.no_name_yet#13, Raspberry_Pi_Zero1.GPIO18
