# Fritzing sketch ssd1306.128x64 (saved by Fritzing 0.9.3b)
breadboards: 2

parts:
  Part1 = OLED Monochrome 128x64 1.3 inch [part_number=938]
  S6 = Pushbutton [package="[SMD]"]
  S7 = Pushbutton [package="[SMD]"]
  Raspberry_Pi_Zero1 = Raspberry Pi Zero
  Part3 = OLED Monochrome 128x64 1.3 inch [part_number=938]
  S8 = Pushbutton [package="[SMD]"]
  S9 = Pushbutton [package="[SMD]"]
  Part6 = PowerBoost 500 Basic  # not connected
  U1 = SWITCH_SPDT [package=kps-1290]  # not connected
  Part7 = Lithium Ion Polymer Battery 3.7v 150mAh [part_number=1317]  # not connected

nets:
  N1: Part1.MOSI_SDA, Raspberry_Pi_Zero1.GPIO10
  N2: Part1.SCLK_SCK, Raspberry_Pi_Zero1.GPIO11
  N3: Part1.DC_SA0, Raspberry_Pi_Zero1.GPIO23
  N4: Part1.RESET, Raspberry_Pi_Zero1.GPIO24
  N5: Part1.CS, Raspberry_Pi_Zero1.GPIO8
  VIN: Part1.VIN, S6.Pin_3, S6.Pin_4, S7.Pin_3, S7.Pin_4, Raspberry_Pi_Zero1.3v3
  GND: Part1.GND, Raspberry_Pi_Zero1.GND
  N6: S6.Pin_1, S6.Pin_2, Raspberry_Pi_Zero1.GPIO21
  N7: S7.Pin_1, S7.Pin_2, Raspberry_Pi_Zero1.GPIO20
  N8: Part3.VIN, S8.Pin_3, S8.Pin_4, S9.Pin_4
  N9: S8.Pin_1, S8.Pin_2
  N10: S9.Pin_1, S9.Pin_2

custom parts:
  OLED Monochrome 128x64 1.3 inch: These displays are small, only about 1.3" diagonal, but very readable due to the high contrast of an OLED display. This display is made of 128x64 individual white OLED pixels, each one is turned on or off by the controller chip. Because the display makes its own light, no backlight is required. This reduces the power required to run the OLED and is why the display has such high contrast; we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
  PowerBoost 500 Basic: The PowerBoost 500 Basic is a little DC/DC boost converter module that can run from 1.8V batteries or higher, and convert the battery output to 5.2V DC for running your 5V projects. At its heart is a TPS61090 boost converter from TI. This boost converter chip has some really nice extras such as low battery detection, 2A internal switch, synchronous conversion, excellent efficiency, and 700KHz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
  Lithium Ion Polymer Battery 3.7v 150mAh: Lithium ion polymer (also known as 'lipo' or 'lipoly') batteries are thin, light and powerful. The output ranges from 4.2V when completely charged to 3.7V. This battery has a capacity of 150mAh for a total of about 0.6 Wh. The batteries come pre-attached with a genuine 2-pin JST-PH connector as shown and include the necessary protection circuitry.
