# Fritzing sketch reflex.game (saved by Fritzing 0.9.3b)
breadboards: 1

parts:
  Raspberry_Pi_1 = Raspberry Pi 3 [part_number=RPI-3-V1.2]
  LED1 = smd LED [color="Red (633nm)" package="1206 [SMD]"]
  S1 = Momentary Switch [package=ksa_sealed_tac_switch]
  R1 = Resistor [tolerance=±5% resistance=330 package="0402 [SMD]"]

nets:
  N1: Raspberry_Pi_1.GIPO27, S1.2
  N2: Raspberry_Pi_1.GIPO18, LED1.anode
  N3: Raspberry_Pi_1.GND, S1.4, R1.Pin_1
  N4: LED1.cathode, R1.Pin_0
