# Fritzing sketch TCP.watch (saved by Fritzing 0.9.3b)

parts:
  Part1 = Adafruit HUZZAH ESP8266 [part_number="Adafruit #2471"]
  Part2 = OLED Monochrome 128x64 1.3 inch [part_number=938]
  Part3 = Adafruit Micro USB Breakout [part_number="Adafruit #1833"]

nets:
  N1: Part1.GPIO14, Part2.MOSI_SDA
  N2: Part1.GPIO12, Part2.SCLK_SCK
  VIN: Part1.VIN, Part2.VIN, Part3.VBUS
  GND: Part1.GND, Part2.GND, Part3.GND
  N3: Part1.GPIO2, Part2.RESET

custom parts:
  Adafruit HUZZAH ESP8266: Add Internet to your next project with an adorable, bite-sized WiFi microcontroller, at a price you like! The ESP8266 processor from Espressif is an 80 MHz microcontroller with a full WiFi front-end (both as client and access point) and TCP/IP stack with DNS support as well. While this chip has been very popular, its also been very difficult to use. Most of the low cost modules are not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
  OLED Monochrome 128x64 1.3 inch: These displays are small, only about 1.3" diagonal, but very readable due to the high contrast of an OLED display. This display is made of 128x64 individual white OLED pixels, each one is turned on or off by the controller chip. Because the display makes its own light, no backlight is required. This reduces the power required to run the OLED and is why the display has such high contrast; we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
  Adafruit Micro USB Breakout: Simple but effective - this breakout board has a USB Micro-B connector, with all 5 pins broken out. Great for pairing with a microcontroller with USB support, or adding USB 5V power to a project. We use a micro-AB connector with through-hole shielding pads for an excellent strong connection - it won't rip off by accident! Comes with one fully assembled and tested micro B breakout PCB and a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
