# Fritzing sketch sunflower.adc.monitoring (saved by Fritzing 0.9.3b)
breadboards: 1

parts:
  Raspberry_Pi_1 = Raspberry Pi 3 [part_number=RPI-3-V1.2]
  Part2 = PowerBoost 1000 Basic
  Part3 = Adafruit USB DC Solar LiPo Charger [part_number="Adafruit #390"]
  U1 = LIPO-2000mAh [package=lipo-2000]  # not connected
  X1 = USB Connectors [package=usb-a-s-nosilk-female]
  IC1 = MCP3008 8-channel 10-bit ADC [part_number=MCP3008]  # not connected
  R1 = TRIMPOT [package=trimpot_pth_s3_lock]
  R2 = Photocell (LDR) [package=THT]
  R3 = Resistor [tolerance=±5% resistance=10k package="2010 [SMD]"]

nets:
  GND: Raspberry_Pi_1.GND, Part2.GND, Part3.GND, X1.GND, R1.CCW, R3.Pin_0
  N1: Raspberry_Pi_1.5V, R2.pin_1
  N2: Part2.5.0V, X1.VBUS
  N3: Part2.VBAT, Part3.LOAD
  N4: Part3.BATT, R1.CW
  N5: R2.pin_0, R3.Pin_1

notes:
  Solar Panel input through the Jack here.
  To the Raspberry PI power (micro USB)

custom parts:
  PowerBoost 1000 Basic: The PowerBoost 1000 is a little DC/DC boost converter module that can run from 1.8V batteries or higher, and convert the battery output to 5.2V DC for running your 5V projects. At its heart is a TPS61030 boost converter from TI. This boost converter chip has some really nice extras such as low battery detection, 4A internal switch, synchronous conversion, excellent efficiency, and 700KHz high-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
  Adafruit USB DC Solar LiPo Charger: Make your projects to go green this summer with our specialized USB/Solar Lithium Ion Polymer Battery charger! This charger is a very unique design, perfect for outdoor projects, or DIY iPod chargers. We've spent over a year testing and tinkering with this charger to come up with a plug and play solution to charging batteries with the sun and we're really pleased with what we ended up with.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
