# Fritzing sketch sunflower.autonomous (saved by Fritzing 0.9.3b)
breadboards: 1

parts:
  J1 = Basic Servo
  J2 = Basic Servo
  Part1 = 16-Channel 12-bit PCA9685 PWM/Servo Driver
  Raspberry_Pi_1 = Raspberry Pi 3 [part_number=RPI-3-V1.2]
  Part2 = PowerBoost 1000 Basic
  Part3 = Adafruit USB DC Solar LiPo Charger [part_number="Adafruit #390"]
  U1 = LIPO-2000mAh [package=lipo-2000]  # not connected
  X1 = USB Connectors [package=usb-a-s-nosilk-female]

nets:
  GND: J1.gnd, J2.gnd, Part1.GND, Raspberry_Pi_1.GND
  VCC: J1.vcc, J2.vcc, Part1.V+, Part1.7
  N1: J1.pulse, Part1.14
  N2: J2.pulse, Part1.15
  N3: Part1.PWRIN, Raspberry_Pi_1.5V
  GND_2: Part2.GND, Part3.GND, X1.GND
  N4: Part2.5.0V, X1.VBUS
  N5: Part2.VBAT, Part3.LOAD

notes:
  Sloar Panel input through the Jack here.
  To the Raspberry PI power (micro USB)

custom parts:
  16-Channel 12-bit PCA9685 PWM/Servo Driver: The Adafruit 16-Channel 12-bit PWM/Servo Driver will drive up to 16 servos over I2C with only 2 pins. The on-board PCA9685 PWM controller will drive all 16 channels simultaneously with no additional processing overhead. What's more, you can chain up to 62 of them to control up to 992 servos - all with the same 2 pins
  PowerBoost 1000 Basic: The PowerBoost 1000 is a little DC/DC boost converter module that can run from 1.8V batteries or higher, and convert the battery output to 5.2V DC for running your 5V projects. At its heart is a TPS61030 boost converter from TI. This boost converter chip has some really nice extras such as low battery detection, 4A internal switch, synchronous conversion, excellent efficiency, and 700KHz high-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
  Adafruit USB DC Solar LiPo Charger: Make your projects to go green this summer with our specialized USB/Solar Lithium Ion Polymer Battery charger! This charger is a very unique design, perfect for outdoor projects, or DIY iPod chargers. We've spent over a year testing and tinkering with this charger to come up with a plug and play solution to charging batteries with the sun and we're really pleased with what we ended up with.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
