# Fritzing sketch sunflower.pwd (saved by Fritzing 0.9.3b)
breadboards: 1

parts:
  J1 = Basic Servo
  J2 = Basic Servo
  Part1 = 16-Channel 12-bit PCA9685 PWM/Servo Driver
  Raspberry_Pi_1 = Raspberry Pi 3 [part_number=RPI-3-V1.2]

nets:
  GND: J1.gnd, J2.gnd, Part1.GND, Raspberry_Pi_1.GND
  VCC: J1.vcc, J2.vcc, Part1.V+, Part1.7
  N1: J1.pulse, Part1.14
  N2: J2.pulse, Part1.15
  N3: Part1.PWRIN, Raspberry_Pi_1.5V

custom parts:
  16-Channel 12-bit PCA9685 PWM/Servo Driver: The Adafruit 16-Channel 12-bit PWM/Servo Driver will drive up to 16 servos over I2C with only 2 pins. The on-board PCA9685 PWM controller will drive all 16 channels simultaneously with no additional processing overhead. What's more, you can chain up to 62 of them to control up to 992 servos - all with the same 2 pins
