# Fritzing sketch FirstTest (saved by Fritzing 0.9.4)
breadboards: 1

parts:
  Raspberry_Pi_1 = Raspberry Pi 3 [part_number=RPI-3-V1.2]
  LED1 = smd LED [color="Red (633nm)" package="1206 [SMD]"]
  R1 = Resistor [tolerance=±5% resistance=330 package="0603 [SMD]"]
  S1 = Pushbutton [package="[SMD]"]

nets:
  N1: Raspberry_Pi_1.GPIO12, S1.Pin_1, S1.Pin_2
  N2: Raspberry_Pi_1.GND, LED1.anode, S1.Pin_3, S1.Pin_4
  N3: Raspberry_Pi_1.GPIO18, R1.Pin_1
  N4: LED1.cathode, R1.Pin_0

notes:
  Led is on pin #18,
  Button on pin #12
  A 330Ω Resistor
