# Fritzing sketch MCP3008 (saved by Fritzing 0.9.4)
breadboards: 1

parts:
  Raspberry_Pi_1 = Raspberry Pi 3 [part_number=RPI-3-V1.2]
  ADC1 = MCP3008 [package=dil16]
  R1 = Rotary Potentiometer (Large) [maximum_resistance=100kΩ package=THT]

nets:
  3V3: Raspberry_Pi_1.3v3, Raspberry_Pi_1.3V3, ADC1.VREF, ADC1.VDD, R1.leg1, R1.leg2
  N1: Raspberry_Pi_1.GIPO10, ADC1.Din
  N2: Raspberry_Pi_1.GIPO9, ADC1.Dout
  N3: Raspberry_Pi_1.GIPO11, ADC1.CLK
  N4: Raspberry_Pi_1.GIPO7, ADC1.CS/SHDN
  N5: Raspberry_Pi_1.GND, ADC1.DGND, ADC1.AGND
  N6: ADC1.CH0, R1.wiper
