# Fritzing sketch RPi-MCP3002-Pot (saved by Fritzing 0.9.3b)
breadboards: 1

parts:
  Raspberry_Pi_1 = Raspberry Pi 3 [part_number=RPI-3-V1.2]
  R1 = TRIMPOT [package=trimpot_pth_s3_lock]
  R2 = Resistor [tolerance=±5% resistance=220 package="0805 [SMD]"]
  MCP3002 = IC, DIP package, 8 pins [chip_label=MCP3002]

nets:
  N1: Raspberry_Pi_1.3v3, R1.CW, MCP3002.pin8
  N2: Raspberry_Pi_1.GPIO25, MCP3002.pin1
  N3: Raspberry_Pi_1.GPIO24, MCP3002.pin5
  N4: Raspberry_Pi_1.GPIO23, MCP3002.pin6
  N5: Raspberry_Pi_1.GPIO18, MCP3002.pin7
  N6: Raspberry_Pi_1.GND, R1.CCW, MCP3002.pin4
  N7: R1.WIPER, R2.Pin_1
  N8: R2.Pin_0, MCP3002.pin2
