# Fritzing sketch RPi-MCP3008 (saved by Fritzing 0.9.3b)
breadboards: 1

parts:
  IC1 = MCP3008 8-channel 10-bit ADC [part_number=MCP3008]
  Raspberry_Pi_1 = Raspberry Pi 3 [part_number=RPI-3-V1.2]

nets:
  N1: IC1.no_name_yet#9, IC1.no_name_yet#14, Raspberry_Pi_1.GND
  N2: IC1.no_name_yet#10, Raspberry_Pi_1.GPIO25
  N3: IC1.no_name_yet#11, Raspberry_Pi_1.GPIO24
  N4: IC1.no_name_yet#12, Raspberry_Pi_1.GPIO23
  N5: IC1.no_name_yet#13, Raspberry_Pi_1.GPIO18
  3V3: IC1.no_name_yet#15, IC1.no_name_yet#16, Raspberry_Pi_1.3v3, Raspberry_Pi_1.3V3

notes:
  8 analog channels available on this side of the MCP3008
