# Fritzing sketch ads1115 (saved by Fritzing 0.9.3b)
breadboards: 1

parts:
  Part1 = Adafruit ADS1115 16Bit I2C ADC [part_number="Adafruit #1085"]
  Raspberry_Pi_1 = Raspberry Pi 3 [part_number=RPI-3-V1.2]

nets:
  N1: Part1.SDA, Raspberry_Pi_1.GPIO2
  N2: Part1.SCL, Raspberry_Pi_1.GPIO3
  GND: Part1.GND, Raspberry_Pi_1.GND
  VDD: Part1.VDD, Raspberry_Pi_1.3v3

notes:
  Channels to read are A0, A1, A2 and/or A3. Grounded.

custom parts:
  Adafruit ADS1115 16Bit I2C ADC: For microcontrollers without an analog-to-digital converter or when you want a higher-precision ADC, the ADS1115 provides 16-bit precision at 860 samples/second over I2C. The chip can be configured as 4 single-ended input channels, or two differential channels. As a nice bonus, it even includes a programmable gain amplifier, up to x16, to help boost up smaller single/differential signals to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
