# Fritzing sketch catapult (saved by Fritzing 0.9.4)

parts:
  Raspberry_Pi_1 = Raspberry Pi 3 [part_number=RPI-3-V1.2]
  M1 = Dagu DGServo 9g (Pan and tilt) [part_number=RS001B]

nets:
  GND: Raspberry_Pi_1.GND, M1.gnd

notes:
  Red: 5V
  Brown: GND
  Orange: PWM Signal
