# Fritzing sketch Membrane3x4MatrixKeypad (saved by Fritzing 0.9.3b)
breadboards: 1

parts:
  KEYPAD1 = Membrane Matrix Keypad
  Raspberry_Pi_1 = Raspberry Pi 3 [part_number=RPI-3-V1.2]

nets:
  N1: KEYPAD1.1, Raspberry_Pi_1.GPIO18
  N2: KEYPAD1.2, Raspberry_Pi_1.GPIO23
  N3: KEYPAD1.3, Raspberry_Pi_1.GPIO24
  N4: KEYPAD1.4, Raspberry_Pi_1.GPIO25
  N5: KEYPAD1.5, Raspberry_Pi_1.GPIO4
  N6: KEYPAD1.6, Raspberry_Pi_1.GPIO17
  N7: KEYPAD1.7, Raspberry_Pi_1.GPIO22

notes:
  Verified.

custom parts:
  Membrane Matrix Keypad: Membrane Matrix 3x4 Keypad
